# Fritzing sketch hmc58883l (saved by Fritzing 0.9.3b)
circuit board: 8.46667cm x 5.64444cm
breadboards: 1

parts:
  Part1 = Arduino Nano (Rev3.0)
  Part2 = Triple Axis Magnetometer - HMC5883 Breakout

nets:
  GND: Part1.GND, Part2.GND
  N1: Part1.A5, Part2.SCL
  N2: Part1.A4, Part2.SDA
  3V3: Part1.3V3, Part2.VCC

// code stored in the sketch: hmctest.ino
#include <Wire.h> //I2C Arduino Library

#define addr 0x0D //I2C Address for The HMC5883

void setup() {

  Serial.begin(9600);
  Wire.begin();


  Wire.beginTransmission(addr); //start talking
  Wire.write(0x0B); // Tell the HMC5883 to Continuously Measure
  Wire.write(0x01); // Set the Register
  Wire.endTransmission();
  Wire.beginTransmission(addr); //start talking
  Wire.write(0x09); // Tell the HMC5883 to Continuously Measure
  Wire.write(0x1D); // Set the Register
  Wire.endTransmission();
}

void loop() {

  int x, y, z; //triple axis data
	float azimuth; //heading angle
  //Tell the HMC what regist to begin writing data into


  Wire.beginTransmission(addr);
  Wire.write(0x00); //start with register 3.
  Wire.endTransmission();

  //Read the data.. 2 bytes for each axis.. 6 total bytes
  Wire.requestFrom(addr, 6);
  if (6 <= Wire.available()) {
	  // DATA OF EACH AXIX IS 16 BIT 2S COMP HENCE MSB IS SHIFTED WITH EIGHT ZEROS AND ORED WITH LSB BYTE
    x = Wire.read(); //MSB  x
    x |= Wire.read() << 8; //LSB  x
    z = Wire.read(); //MSB  z
    z |= Wire.read() << 8; //LSB z
    y = Wire.read(); //MSB y
    y |= Wire.read() << 8; //LSB y
  }
	 azimuth = atan2(y,x) * 180.0/PI;
   if (azimuth < 0 )azimuth=360.0+ azimuth;  //compute heading using 
  // Show Values
  Serial.print("X Value: ");
  Serial.println(x);
  Serial.print("Y Value: ");
  Serial.println(y);
  Serial.print("Z Value: ");
  Serial.println(z);
	Serial.print("Azimuth: ");
	Serial.print(azimuth);
  Serial.println();

  delay(500);
}
