# Fritzing sketch 74hc165 (saved by Fritzing 0.9.3b)
breadboards: 1

parts:
  Part1 = Arduino Uno (Rev3)
  U1 = 74HC165 [part_number=SN74LS165 package="DIP16 [THT]"]
  C1 = Electrolytic Capacitor [capacitance=1µF package="100 mil [THT, electrolytic]"]
  S1 = Pushbutton [package="[THT]"]
  S2 = Pushbutton [package="[THT]"]
  S3 = Pushbutton [package="[THT]"]
  S4 = Pushbutton [package="[THT]"]
  S5 = Pushbutton [package="[THT]"]
  S6 = Pushbutton [package="[THT]"]
  S7 = Pushbutton [package="[THT]"]
  S8 = Pushbutton [package="[THT]"]
  R1 = Resistor [tolerance=±5% resistance=10k package=THT]
  R2 = Resistor [tolerance=±5% resistance=10k package=THT]
  R3 = Resistor [tolerance=±5% resistance=10k package=THT]
  R4 = Resistor [tolerance=±5% resistance=10k package=THT]
  R5 = Resistor [tolerance=±5% resistance=10k package=THT]
  R6 = Resistor [tolerance=±5% resistance=10k package=THT]
  R7 = Resistor [tolerance=±5% resistance=10k package=THT]
  R8 = Resistor [tolerance=±5% resistance=10k package=THT]
  C2 = Ceramic Capacitor [capacitance=100nF package="100 mil [THT, multilayer]"]

nets:
  GND: Part1.GND, U1.GND, U1.MR, C1.-, R1.Pin_1, R2.Pin_1, R3.Pin_1, R4.Pin_1, R5.Pin_1, R6.Pin_1, R7.Pin_1, R8.Pin_1, C2.1
  N1: Part1.D2, U1.Q1, C2.0
  N2: Part1.D3_PWM, U1.Q2
  N3: Part1.D4, U1.Q7'
  5V: Part1.5V, U1.VCC, C1.+, S1.Pin_1, S1.Pin_2, S2.Pin_1, S2.Pin_2, S3.Pin_1, S3.Pin_2, S4.Pin_1, S4.Pin_2, S5.Pin_1, S5.Pin_2, S6.Pin_1, S6.Pin_2, S7.Pin_1, S7.Pin_2, S8.Pin_1, S8.Pin_2
  N4: U1.Q3, S6.Pin_3, S6.Pin_4, R7.Pin_0
  N5: U1.Q4, S7.Pin_3, S7.Pin_4, R1.Pin_0
  N6: U1.Q5, S8.Pin_3, S8.Pin_4, R8.Pin_0
  N7: U1.SH_CP, S1.Pin_3, S1.Pin_4, R2.Pin_0
  N8: U1.ST_CP, S2.Pin_3, S2.Pin_4, R3.Pin_0
  N9: U1.OE, S3.Pin_3, S3.Pin_4, R4.Pin_0
  N10: U1.DS, S4.Pin_3, S4.Pin_4, R5.Pin_0
  N11: U1.Q0, S5.Pin_3, S5.Pin_4, R6.Pin_0

custom parts:
  74HC165: 8-bit parallel-load shift registers

// code stored in the sketch: Untitled.ino
//example for 74_165 (PISO) using IO_EXPANDER.

#include<IOexpander.h>

//create an class object io.
IOexpander io(1,4,3,2); // IOexpander io(number of registers ,data_in,clock,latch);
void setup() {
Serial.begin(115200);
}

void loop() {
	
// reading all the input pins : readAll();
Serial.println(io.readAll(),BIN);

// reading status of single pin : readPin(pin number);
//pin number should not exceeds 8 * number of registers
//MSB- H=D8 G=D7 F=D6 E=D5 D=D4 C=D3 B=D2 A=D1 -LSB
Serial.println(io.readPin(4));

delay(1000);

}
