# Fritzing sketch connections (saved by Fritzing 0.9.3b)
breadboards: 2

parts:
  Part1 = Arduino Uno (Rev3)
  U1 = 74HC595 [package="DIP16 [THT]"]
  U2 = 74HC595 [package="DIP16 [THT]"]
  LED1 = LED - 5mm [color="Red (633nm)" package="5 mm [THT]"]
  LED2 = LED - 5mm [color="Red (633nm)" package="5 mm [THT]"]
  LED3 = LED - 5mm [color="Red (633nm)" package="5 mm [THT]"]
  LED4 = LED - 5mm [color="Red (633nm)" package="5 mm [THT]"]
  LED5 = LED - 5mm [color="Red (633nm)" package="5 mm [THT]"]
  LED6 = LED - 5mm [color="Red (633nm)" package="5 mm [THT]"]
  LED7 = LED - 5mm [color="Red (633nm)" package="5 mm [THT]"]
  LED8 = LED - 5mm [color="Red (633nm)" package="5 mm [THT]"]
  LED9 = LED - 5mm [color="Red (633nm)" package="5 mm [THT]"]
  LED10 = LED - 5mm [color="Red (633nm)" package="5 mm [THT]"]
  LED11 = LED - 5mm [color="Red (633nm)" package="5 mm [THT]"]
  LED12 = LED - 5mm [color="Red (633nm)" package="5 mm [THT]"]
  LED13 = LED - 5mm [color="Red (633nm)" package="5 mm [THT]"]
  LED14 = LED - 5mm [color="Red (633nm)" package="5 mm [THT]"]
  LED15 = LED - 5mm [color="Red (633nm)" package="5 mm [THT]"]
  LED16 = LED - 5mm [color="Red (633nm)" package="5 mm [THT]"]
  R1 = Resistor [tolerance=±5% resistance=220 package=THT]
  R2 = Resistor [tolerance=±5% resistance=220 package=THT]
  R3 = Resistor [tolerance=±5% resistance=220 package=THT]
  R4 = Resistor [tolerance=±5% resistance=220 package=THT]
  R5 = Resistor [tolerance=±5% resistance=220 package=THT]
  R6 = Resistor [tolerance=±5% resistance=220 package=THT]
  R7 = Resistor [tolerance=±5% resistance=220 package=THT]
  R8 = Resistor [tolerance=±5% resistance=220 package=THT]
  R9 = Resistor [tolerance=±5% resistance=220 package=THT]
  R10 = Resistor [tolerance=±5% resistance=220 package=THT]
  R11 = Resistor [tolerance=±5% resistance=220 package=THT]
  R12 = Resistor [tolerance=±5% resistance=220 package=THT]
  R13 = Resistor [tolerance=±5% resistance=220 package=THT]
  R14 = Resistor [tolerance=±5% resistance=220 package=THT]
  R15 = Resistor [tolerance=±5% resistance=220 package=THT]
  R16 = Resistor [tolerance=±5% resistance=220 package=THT]
  R17 = Resistor [tolerance=±5% resistance=10k package=THT]
  C1 = Ceramic Capacitor [capacitance=100nF package="100 mil [THT, multilayer]"]

nets:
  N1: Part1.D9_PWM, U1.OE, U2.OE
  N2: Part1.D3_PWM, U1.DS
  N3: Part1.D4, U1.ST_CP, U2.ST_CP, R17.Pin_1, C1.1
  N4: Part1.D5_PWM, U1.SH_CP, U2.SH_CP
  VCC: Part1.5V, U1.MR, U1.VCC, U2.MR, U2.VCC
  GND: Part1.GND, U1.GND, U2.GND, LED1.cathode, LED2.cathode, LED3.cathode, LED4.cathode, LED5.cathode, LED6.cathode, LED7.cathode, LED8.cathode, LED9.cathode, LED10.cathode, LED11.cathode, LED12.cathode, LED13.cathode, LED14.cathode, LED15.cathode, LED16.cathode, R17.Pin_0, C1.0
  N5: U1.Q1, R12.Pin_0
  N6: U1.Q2, R13.Pin_0
  N7: U1.Q3, R14.Pin_0
  N8: U1.Q4, R15.Pin_0
  N9: U1.Q5, R16.Pin_0
  N10: U1.Q6, R10.Pin_0
  N11: U1.Q7, R9.Pin_0
  N12: U1.Q7', U2.DS
  N13: U1.Q0, R11.Pin_0
  N14: U2.Q1, R7.Pin_0
  N15: U2.Q2, R6.Pin_0
  N16: U2.Q3, R5.Pin_0
  N17: U2.Q4, R4.Pin_0
  N18: U2.Q5, R3.Pin_0
  N19: U2.Q6, R2.Pin_0
  N20: U2.Q7, R1.Pin_0
  N21: U2.Q0, R8.Pin_0
  N22: LED1.anode, R1.Pin_1
  N23: LED2.anode, R11.Pin_1
  N24: LED3.anode, R12.Pin_1
  N25: LED4.anode, R13.Pin_1
  N26: LED5.anode, R14.Pin_1
  N27: LED6.anode, R15.Pin_1
  N28: LED7.anode, R16.Pin_1
  N29: LED8.anode, R10.Pin_1
  N30: LED9.anode, R9.Pin_1
  N31: LED10.anode, R2.Pin_1
  N32: LED11.anode, R3.Pin_1
  N33: LED12.anode, R4.Pin_1
  N34: LED13.anode, R5.Pin_1
  N35: LED14.anode, R6.Pin_1
  N36: LED15.anode, R7.Pin_1
  N37: LED16.anode, R8.Pin_1
